# Fritzing sketch Metro_temp_hum_oled (saved by Fritzing 0.9.3b)
breadboards: 1

parts:
  Onderdeel1 = Adafruit Si7021 Temp Humidity [part_number="Adafruit #3251"]
  Oled = OLED Monochrome 128x64 0.96 inch [part_number=326]
  Onderdeel3 = Adafruit Metro M0 Express

nets:
  N1: Onderdeel1.SDA, Oled.MOSI_SDA, Onderdeel3.SDA
  N2: Onderdeel1.SCL, Oled.SCLK_SCK, Onderdeel3.SCL
  GND: Onderdeel1.GND, Oled.GND, Onderdeel3.GND
  VIN: Onderdeel1.VIN, Oled.VIN, Onderdeel3.+5V
  N3: Oled.RESET, Onderdeel3.D4

custom parts:
  Adafruit Si7021 Temp Humidity: It's summer and you're sweating and your hair's all frizzy and all you really want to know is why the weatherman said this morning that today's relative humidity would max out at a perfectly reasonable 42% when it feels more like 77%. Enter the Si7021 Temperature + Humidity Sensor - the best way to prove the weatherman wrong! This lovely sensor for Silicon labs has ± 3% relative humidity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
  OLED Monochrome 128x64 0.96 inch: These displays are small, only about 1" diameter, but very readable due to the high contrast of an OLED display. This display is made of 128x64 individual white OLED pixels, each one is turned on or off by the controller chip. Because the display makes its own light, no backlight is required. This reduces the power required to run the OLED and is why the display has such high contrast; we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
  Adafruit Metro M0 Express: Metro is our series of microcontroller boards for use with the Arduino IDE. This new Metro board looks a whole lot like our original Metro 328, but with a huge upgrade. Instead of the ATmega328, this Metro features a ATSAMD21G18 chip, an ARM Cortex M0+. It's our first Metro that is designed for use with CircuitPython! CircuitPython is our beginner-oriented flavor of MicroPython - and as the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
